# Fritzing sketch MEx-Raspi-Connector (saved by Fritzing 0.9.3b)
circuit board: 3.78896cm x 5.47664cm
breadboards: 1

parts:
  Raspberry_Pi_3 = Raspberry Pi 3 [part_number=RPI-3-V1.2]
  EXPW = Battery block 9V
  MG995 = Basic Servo
  90GL = Basic Servo
  90GU = Basic Servo
  L9110s = L9110 H-bridge module [part_number="L9110 H-bridge"]
  M1 = DC Motor
  M2 = DC Motor

nets:
  N1: Raspberry_Pi_3.GIPO21, L9110s.A-IA
  N2: Raspberry_Pi_3.GIPO20, L9110s.A-IB
  N3: Raspberry_Pi_3.GIPO16, L9110s.B-IA
  N4: Raspberry_Pi_3.GIPO12, L9110s.B-IB
  GND: Raspberry_Pi_3.GND, EXPW.-, MG995.gnd, 90GL.gnd, 90GU.gnd, L9110s.GND
  N5: Raspberry_Pi_3.GIPO18, 90GU.pulse
  N6: Raspberry_Pi_3.GIPO15, 90GL.pulse
  N7: Raspberry_Pi_3.GIPO14, MG995.pulse
  VCC: Raspberry_Pi_3.5V, MG995.vcc, 90GL.vcc, 90GU.vcc
  N8: EXPW.+, L9110s.VCC
  N9: L9110s.MOTOR_A-A, M1.pin_2
  N10: L9110s.MOTOR_A-B, M1.pin_1
  N11: L9110s.MOTOR_B-A, M2.pin_2
  N12: L9110s.MOTOR_B-B, M2.pin_1
